// Logisim project alu.circ as structural Verilog: 2 circuits, main circuit ALU_4
module ALU_4 (
  input  [3:0] A,
  input  [3:0] B,
  input  [2:0] S,
  output [3:0] F
);

  wire [3:0] adder_1_out, and_1_out, or_1_out, subtractor_1_out;

  Adder #(.width(4)) adder_1 (.a(A), .b(B), .out(adder_1_out));  // open: cin, cout
  Subtractor #(.width(4)) subtractor_1 (.a(A), .b(B), .out(subtractor_1_out));  // open: bin, bout
  assign and_1_out = A & B;  // AND_Gate and_1, 4 bits wide
  assign or_1_out = A | B;  // OR_Gate or_1, 4 bits wide
  Multiplexer #(.select(3), .width(4)) multiplexer_1 (
    .in0(adder_1_out), .in1(subtractor_1_out), .in2(and_1_out), .in3(or_1_out), .out(F), .sel(S));  // open: in4, in5, in6, in7
endmodule

module GP (
  output [7:0] out_1
);

  wire and_1_out, clock_1_out, comparator_1_eq, not_1_out, not_2_out, or_1_out;
  wire [3:0] adder_1_out, multiplexer_1_out, PC_q;
  wire [7:0] adder_2_out, register_1_q, ROM16_data;

  Multiplexer #(.width(4)) multiplexer_1 (
    .in0(ROM16_data[3:0]), .in1(adder_1_out), .out(multiplexer_1_out), .sel(ROM16_data[7]));
  Register #(.width(4)) PC (.D(multiplexer_1_out), .en(and_1_out), .clk(clock_1_out), .Q(PC_q), .clr(1'b0));
  Clock clock_1 (.out(clock_1_out));
  Adder #(.width(4)) adder_1 (.a(PC_q), .b(4'b0001), .out(adder_1_out));  // open: cin, cout
  and and_1 (and_1_out, not_1_out, or_1_out);
  ROM #(.addrWidth(4)) ROM16 (.addr(PC_q), .data(ROM16_data));
  not not_1 (not_1_out, ROM16_data[7]);
  or or_1 (or_1_out, ROM16_data[4], not_2_out);
  not not_2 (not_2_out, comparator_1_eq);
  Register register_1 (.D(adder_2_out), .en(ROM16_data[6]), .clk(clock_1_out), .Q(register_1_q), .clr(ROM16_data[5]));
  assign out_1 = ROM16_data[4] ? register_1_q : 8'bz;  // Controlled_Buffer controlled_buffer_1
  Adder adder_2 (.a(register_1_q), .b(8'h1), .out(adder_2_out));  // open: cin, cout
  Comparator comparator_1 (.a(register_1_q), .b(8'ha), .eq(comparator_1_eq));  // open: gt, lt

  // Notes on the sheet:
  //   contents of ROM16 (hex, n*v repeats v):
  //   a0 90 c0 80 1 15
endmodule
