// Logisim project alu.circ as structural Verilog: 1 circuit, main circuit GP
module GP (
  output [7:0] COUNT
);

  wire and_1_out, clock_1_out, comparator_1_eq, not_1_out, not_2_out, or_1_out, RESET_out;
  wire [3:0] adder_1_out, multiplexer_1_out, PC_q, ROM16_data;
  wire [7:0] ACC_q, adder_2_out;
  wire [7:4] ROM16_data_2;

  Button RESET (.out(RESET_out));
  Multiplexer #(.width(4)) multiplexer_1 (
    .in0(adder_1_out), .in1(ROM16_data), .out(multiplexer_1_out), .sel(and_1_out));
  Register #(.width(4)) PC (.D(multiplexer_1_out), .en(1'b1), .clk(clock_1_out), .Q(PC_q), .clr(RESET_out));
  Clock clock_1 (.out(clock_1_out));
  Adder #(.width(4)) adder_1 (.a(PC_q), .b(4'b0001), .out(adder_1_out));  // open: cin, cout
  and and_1 (and_1_out, not_1_out, or_1_out);
  ROM #(.addrWidth(4)) ROM16 (.addr(PC_q), .data({ROM16_data_2, ROM16_data}));
  or or_1 (or_1_out, ROM16_data_2[4], not_2_out);
  not not_1 (not_1_out, ROM16_data_2[7]);
  not not_2 (not_2_out, comparator_1_eq);
  Register ACC (.D(adder_2_out), .en(ROM16_data_2[6]), .clk(clock_1_out), .Q(ACC_q), .clr(ROM16_data_2[5]));
  assign COUNT = ROM16_data_2[4] ? ACC_q : 8'bz;  // Controlled_Buffer controlled_buffer_1
  Adder adder_2 (.a(ACC_q), .b(8'h1), .out(adder_2_out));  // open: cin, cout
  Comparator comparator_1 (.a(ACC_q), .b(8'ha), .eq(comparator_1_eq));  // open: gt, lt
  Hex_Digit_Display hex_digit_display_1 (.value(COUNT[3:0]));  // open: dp

  // Notes on the sheet:
  //   PC_load
  //   contents of ROM16 (hex, n*v repeats v):
  //   a0 90 c0 80 1 15
  //   SEQ
  //   CLR_A
  //   LD_A
  //   OUT
  //   NEQ_10
endmodule
